// Digital circuit 555 timer.dig as structural Verilog
module _555_timer (
  input  _555_Timer,
  output D0,
  output D1,
  output D2,
  output D3,
  output E0,
  output E1,
  output E2,
  output E3,
  output A0,
  output A1,
  output A2,
  output A3,
  output B3,
  output B2,
  output B1,
  output B0,
  output C0,
  output C1,
  output C2,
  output C3,
  output _10_s_Clock_Pulse,
  output _100_s_Clock_Pulse,
  output Clock_Pulse
);

  wire _7400_1_pin6, _7400_2_pin3, _7404_1_pin1, _7404_1_pin2, _7404_1_pin3, _7404_1_pin4, _7404_1_pin10,
       _7404_1_pin12, _74162_2_pin7, Dec1_pin9, Dec1_pin10, Dec1_pin11, Dec1_pin12, Dec1_pin13, Dec1_pin14,
       Dec1_pin15, Dec2_pin9, Dec2_pin10, Dec2_pin11, Dec2_pin12, Dec2_pin13, Dec2_pin14, Dec2_pin15,
       Dec3_pin9, Dec3_pin10, Dec3_pin11, Dec3_pin12, Dec3_pin13, Dec3_pin14, Dec3_pin15;

  _7400 _7400_1 (
    .pin1(1'b0), .pin2(1'b0), .pin4(B0), .pin5(B0), .pin6(_7400_1_pin6), .pin7(1'b0),
    .pin8(_10_s_Clock_Pulse), .pin9(_7400_1_pin6), .pin10(_7400_1_pin6), .pin12(1'b0), .pin13(1'b0),
    .pin14(1'b1));  // open: pin3, pin11
  _7404 _7404_1 (
    .pin1(_7404_1_pin1), .pin2(_7404_1_pin2), .pin3(_7404_1_pin3), .pin4(_7404_1_pin4), .pin5(1'b0),
    .pin7(1'b0), .pin9(1'b0), .pin10(_7404_1_pin10), .pin11(D2), .pin12(_7404_1_pin12), .pin13(D0),
    .pin14(1'b1));  // open: pin6, pin8
  _7447 Dec2 (
    .pin1(B1), .pin2(B2), .pin3(1'b1), .pin4(1'b1), .pin5(1'b1), .pin6(B3), .pin7(B0), .pin8(1'b0),
    .pin9(Dec2_pin9), .pin10(Dec2_pin10), .pin11(Dec2_pin11), .pin12(Dec2_pin12), .pin13(Dec2_pin13),
    .pin14(Dec2_pin14), .pin15(Dec2_pin15), .pin16(1'b1));
  _74162 _74162_1 (
    .pin1(1'b1), .pin2(_7400_1_pin6), .pin3(1'b0), .pin4(1'b0), .pin5(1'b0), .pin6(1'b0),
    .pin7(_100_s_Clock_Pulse), .pin8(1'b0), .pin9(1'b1), .pin10(1'b1), .pin11(C3), .pin12(C2), .pin13(C1),
    .pin14(C0), .pin16(1'b1));  // open: pin15
  _7400 _7400_2 (
    .pin1(_7404_1_pin2), .pin2(_7404_1_pin4), .pin3(_7400_2_pin3), .pin4(1'b0), .pin5(1'b0), .pin7(1'b0),
    .pin8(_7404_1_pin1), .pin9(D3), .pin10(_7404_1_pin10), .pin11(_7404_1_pin3), .pin12(D1),
    .pin13(_7404_1_pin12), .pin14(1'b1));  // open: pin6
  _7447 Dec3 (
    .pin1(C1), .pin2(C2), .pin3(1'b1), .pin4(1'b1), .pin5(1'b1), .pin6(C3), .pin7(C0), .pin8(1'b0),
    .pin9(Dec3_pin9), .pin10(Dec3_pin10), .pin11(Dec3_pin11), .pin12(Dec3_pin12), .pin13(Dec3_pin13),
    .pin14(Dec3_pin14), .pin15(Dec3_pin15), .pin16(1'b1));
  _74161 _74161_1 (
    .pin1(_7400_2_pin3), .pin2(_555_Timer), .pin3(1'b0), .pin4(1'b0), .pin5(1'b0), .pin6(1'b0), .pin7(1'b1),
    .pin8(1'b0), .pin9(1'b1), .pin10(1'b1), .pin11(D3), .pin12(D2), .pin13(D1), .pin14(D0), .pin16(1'b1));  // open: pin15
  Seven_Seg #(.commonCathode("true"), .commonConnectionType("anode")) seven_seg_1 (
    .a(Dec3_pin13), .b(Dec3_pin12), .c(Dec3_pin11), .d(Dec3_pin10), .e(Dec3_pin9), .f(Dec3_pin15),
    .g(Dec3_pin14), .dp(1'b0), .common(1'b1));
  Seven_Seg #(.commonCathode("true"), .commonConnectionType("anode")) seven_seg_2 (
    .a(Dec2_pin13), .b(Dec2_pin12), .c(Dec2_pin11), .d(Dec2_pin10), .e(Dec2_pin9), .f(Dec2_pin15),
    .g(Dec2_pin14), .dp(1'b0), .common(1'b1));
  _74162 _74162_2 (
    .pin1(1'b1), .pin2(_555_Timer), .pin3(1'b0), .pin4(1'b0), .pin5(1'b0), .pin6(1'b0), .pin7(_74162_2_pin7),
    .pin8(1'b0), .pin9(1'b1), .pin10(1'b1), .pin11(B3), .pin12(B2), .pin13(B1), .pin14(B0),
    .pin15(_100_s_Clock_Pulse), .pin16(1'b1));
  Seven_Seg #(.commonCathode("true"), .commonConnectionType("anode")) seven_seg_3 (
    .a(Dec1_pin13), .b(Dec1_pin12), .c(Dec1_pin11), .d(Dec1_pin10), .e(Dec1_pin9), .f(Dec1_pin15),
    .g(Dec1_pin14), .dp(1'b0), .common(1'b1));
  _7447 Dec1 (
    .pin1(A1), .pin2(A2), .pin3(1'b1), .pin4(1'b1), .pin5(1'b1), .pin6(A3), .pin7(A0), .pin8(1'b0),
    .pin9(Dec1_pin9), .pin10(Dec1_pin10), .pin11(Dec1_pin11), .pin12(Dec1_pin12), .pin13(Dec1_pin13),
    .pin14(Dec1_pin14), .pin15(Dec1_pin15), .pin16(1'b1));
  _74161 _74161_2 (
    .pin1(1'b1), .pin2(_555_Timer), .pin3(1'b0), .pin4(1'b0), .pin5(1'b0), .pin6(1'b0), .pin7(1'b1),
    .pin8(1'b0), .pin9(1'b1), .pin10(1'b1), .pin11(E3), .pin12(E2), .pin13(E1), .pin14(E0), .pin16(1'b1));  // open: pin15
  _74162 _74162_3 (
    .pin1(1'b1), .pin2(_555_Timer), .pin3(1'b0), .pin4(1'b0), .pin5(1'b0), .pin6(1'b0), .pin7(1'b1),
    .pin8(1'b0), .pin9(1'b1), .pin10(1'b1), .pin11(A3), .pin12(A2), .pin13(A1), .pin14(A0),
    .pin15(_74162_2_pin7), .pin16(1'b1));

  assign Clock_Pulse = _555_Timer;

  // Notes on the sheet:
  //   Cascaded Counter #3
  //   100s
  //   Cascaded Counter #2
  //   10s
  //   Counter #1
  //            0 - 9
  //   Counter #2
  //   0 - 15
  //   Cascaded Counter #1
  //   1s
endmodule
