// Digital circuit 8 bit register.dig as structural Verilog
module _8_bit_register (
  input  Load,
  input  Clock,
  input  Enable,
  input  d7,
  input  d6,
  input  d5,
  input  d4,
  input  d3,
  input  d2,
  input  d1,
  input  d0,
  output bus0,
  output bus1,
  output bus2,
  output bus3,
  output bus4,
  output bus5,
  output bus6,
  output bus7
);

  wire _74245_ap_ver_1_p3, _74245_ap_ver_1_p5, _74245_ap_ver_1_p7, _74245_ap_ver_1_p9, _74245_ap_ver_1_p11,
       _74245_ap_ver_1_p13, _74245_ap_ver_1_p15, _74245_ap_ver_1_p17;

  // _74245_ap_ver _74245_ap_ver_1: pin names not known; wires that end beside it: 1'b1, Enable, _74245_ap_ver_1_p3, bus7, _74245_ap_ver_1_p5, bus6, _74245_ap_ver_1_p7, bus5, _74245_ap_ver_1_p9, bus4, _74245_ap_ver_1_p11, bus3, _74245_ap_ver_1_p13, bus2, _74245_ap_ver_1_p15, bus1, _74245_ap_ver_1_p17, bus0, 1'b0
  _74173 _74173_1 (
    .pin1(1'b0), .pin2(1'b0), .pin3(_74245_ap_ver_1_p3), .pin4(_74245_ap_ver_1_p5),
    .pin5(_74245_ap_ver_1_p7), .pin6(_74245_ap_ver_1_p9), .pin7(Clock), .pin8(1'b0), .pin9(Load),
    .pin10(Load), .pin11(d3), .pin12(d2), .pin13(d1), .pin14(d0), .pin15(1'b0), .pin16(1'b1));
  _74173 _74173_2 (
    .pin1(1'b0), .pin2(1'b0), .pin3(_74245_ap_ver_1_p11), .pin4(_74245_ap_ver_1_p13),
    .pin5(_74245_ap_ver_1_p15), .pin6(_74245_ap_ver_1_p17), .pin7(Clock), .pin8(1'b0), .pin9(Load),
    .pin10(Load), .pin11(d7), .pin12(d6), .pin13(d5), .pin14(d4), .pin15(1'b0), .pin16(1'b1));

  // Notes on the sheet:
  //   Input
  //   Data Bus
endmodule
