// Digital circuit 74245_ap_ver.dig as structural Verilog
module _74245_ap_ver (
  input  OE,
  input  A1,
  input  A2,
  input  A3,
  input  A4,
  input  A5,
  input  A6,
  input  A7,
  input  A8,
  input  VCC,
  input  GND,
  output B1,
  output B2,
  output B3,
  output B4,
  output B5,
  output B6,
  output B7,
  output B8
);

  PowerSupply powersupply_1 (.VDD(VCC), .GND(GND));
  assign B1 = OE ? A1 : 1'bz;  // Driver driver_1
  assign B2 = OE ? A2 : 1'bz;  // Driver driver_2
  assign B3 = OE ? A3 : 1'bz;  // Driver driver_3
  assign B4 = OE ? A4 : 1'bz;  // Driver driver_4
  assign B5 = OE ? A5 : 1'bz;  // Driver driver_5
  assign B6 = OE ? A6 : 1'bz;  // Driver driver_6
  assign B7 = OE ? A7 : 1'bz;  // Driver driver_7
  assign B8 = OE ? A8 : 1'bz;  // Driver driver_8

  // Notes on the sheet:
  //   OE: pin 1
  //   A1: pin 2
  //   A2: pin 3
  //   A3: pin 4
  //   A4: pin 5
  //   A5: pin 6
  //   A6: pin 7
  //   A7: pin 8
  //   A8: pin 9
  //   VCC: pin 20, default 1
  //   GND: pin 10
endmodule
