// Digital circuit 74273 8 bit register.dig as structural Verilog
module _74273_8_bit_register (
  input  d7,
  input  d6,
  input  d5,
  input  d4,
  input  d3,
  input  d2,
  input  d1,
  input  d0,
  input  Load,
  input  Clock,
  input  Enable,
  output bus0,
  output bus1,
  output bus2,
  output bus3,
  output bus4,
  output bus5,
  output bus6,
  output bus7
);

  wire _74273_1_pin2, _74273_1_pin5, _74273_1_pin6, _74273_1_pin9, _74273_1_pin12, _74273_1_pin15,
       _74273_1_pin16, _74273_1_pin19, and_1_out, not_1_out;

  and and_1 (and_1_out, not_1_out, Clock);
  not not_1 (not_1_out, Load);
  _74273 _74273_1 (
    .pin1(1'b1), .pin2(_74273_1_pin2), .pin3(d0), .pin4(d1), .pin5(_74273_1_pin5), .pin6(_74273_1_pin6),
    .pin7(d2), .pin8(d3), .pin9(_74273_1_pin9), .pin10(1'b0), .pin11(and_1_out), .pin12(_74273_1_pin12),
    .pin13(d4), .pin14(d5), .pin15(_74273_1_pin15), .pin16(_74273_1_pin16), .pin17(d6), .pin18(d7),
    .pin19(_74273_1_pin19), .pin20(1'b1));
  // _74245_ap_ver _74245_ap_ver_1: pin names not known; wires that end beside it: 1'b1, Enable, _74273_1_pin2, bus7, _74273_1_pin5, bus6, _74273_1_pin6, bus5, _74273_1_pin9, bus4, _74273_1_pin12, bus3, _74273_1_pin15, bus2, _74273_1_pin16, bus1, _74273_1_pin19, bus0, 1'b0

  // Notes on the sheet:
  //   Input
  //   Data Bus
endmodule
