// Digital circuit 74374 8 bit register.dig as structural Verilog
module _74374_8_bit_register (
  input  d7,
  input  d6,
  input  d5,
  input  d4,
  input  d3,
  input  d2,
  input  d1,
  input  d0,
  input  Load,
  input  Clock,
  input  Enable,
  output bus0,
  output bus1,
  output bus2,
  output bus3,
  output bus4,
  output bus5,
  output bus6,
  output bus7
);

  wire _74374_1_pin1, and_1_out, not_1_out;

  and and_1 (and_1_out, not_1_out, Clock);
  not not_1 (not_1_out, Load);
  _74374 _74374_1 (
    .pin1(_74374_1_pin1), .pin2(bus0), .pin3(d0), .pin4(d1), .pin5(bus1), .pin6(bus2), .pin7(d2), .pin8(d3),
    .pin9(bus3), .pin10(1'b0), .pin11(and_1_out), .pin12(bus4), .pin13(d4), .pin14(d5), .pin15(bus5),
    .pin16(bus6), .pin17(d6), .pin18(d7), .pin19(bus7), .pin20(1'b1));
  not not_2 (_74374_1_pin1, Enable);

  // Notes on the sheet:
  //   Input
  //   Data Bus
endmodule
