// Digital circuit 74574 8 bit register.dig as structural Verilog
module _74574_8_bit_register (
  input  d7,
  input  d6,
  input  d5,
  input  d4,
  input  d3,
  input  d2,
  input  d1,
  input  d0,
  input  Load,
  input  Clock,
  input  Enable,
  output bus7,
  output bus6,
  output bus5,
  output bus4,
  output bus3,
  output bus2,
  output bus1,
  output bus0
);

  wire _74574_1_pin1, and_1_out, not_1_out;

  and and_1 (and_1_out, not_1_out, Clock);
  not not_1 (not_1_out, Load);
  _74574 _74574_1 (
    .pin1(_74574_1_pin1), .pin2(d0), .pin3(d1), .pin4(d2), .pin5(d3), .pin6(d4), .pin7(d5), .pin8(d6),
    .pin9(d7), .pin10(1'b0), .pin11(and_1_out), .pin12(bus7), .pin13(bus6), .pin14(bus5), .pin15(bus4),
    .pin16(bus3), .pin17(bus2), .pin18(bus1), .pin19(bus0), .pin20(1'b1));
  not not_2 (_74574_1_pin1, Enable);

  // Notes on the sheet:
  //   Data Bus
  //   Input
endmodule
