// Digital circuit 8 bit register.dig as structural Verilog
module _8_bit_register (
  input  Clear,
  input  Load,
  input  Clock,
  input  Enable,
  input  d7,
  input  d6,
  input  d5,
  input  d4,
  input  d3,
  input  d2,
  input  d1,
  input  d0,
  output bit0,
  output bit1,
  output bit2,
  output bit3,
  output bit4,
  output bit5,
  output bit6,
  output bit7,
  output bus7,
  output bus6,
  output bus5,
  output bus4,
  output bus3,
  output bus2,
  output bus1,
  output bus0
);

  _74245 _74245_1 (
    .pin1(1'b1), .pin2(bit0), .pin3(bit1), .pin4(bit2), .pin5(bit3), .pin6(bit4), .pin7(bit5), .pin8(bit6),
    .pin9(bit7), .pin10(1'b0), .pin11(bus7), .pin12(bus6), .pin13(bus5), .pin14(bus4), .pin15(bus3),
    .pin16(bus2), .pin17(bus1), .pin18(bus0), .pin19(Enable), .pin20(1'b1));
  _74173 _74173_1 (
    .pin1(1'b0), .pin2(1'b0), .pin3(bit0), .pin4(bit1), .pin5(bit2), .pin6(bit3), .pin7(Clock), .pin8(1'b0),
    .pin9(Load), .pin10(Load), .pin11(d3), .pin12(d2), .pin13(d1), .pin14(d0), .pin15(Clear), .pin16(1'b1));
  _74173 _74173_2 (
    .pin1(1'b0), .pin2(1'b0), .pin3(bit4), .pin4(bit5), .pin5(bit6), .pin6(bit7), .pin7(Clock), .pin8(1'b0),
    .pin9(Load), .pin10(Load), .pin11(d7), .pin12(d6), .pin13(d5), .pin14(d4), .pin15(Clear), .pin16(1'b1));

  // Notes on the sheet:
  //   Input
  //   Register Data
  //   Data Bus
endmodule
