// Digital circuit ALU.dig as structural Verilog
module ALU (
  input  b0,
  input  b1,
  input  b2,
  input  b3,
  input  b4,
  input  b5,
  input  b6,
  input  b7,
  input  a0,
  input  a1,
  input  a2,
  input  a3,
  input  a4,
  input  a5,
  input  a6,
  input  a7,
  input  Subtract,
  output c7,
  output c6,
  output c5,
  output c4,
  output c3,
  output c2,
  output c1,
  output c0
);

  wire _7486_1_pin3, _7486_1_pin6, _7486_1_pin8, _7486_1_pin11, _7486_2_pin3, _7486_2_pin6, _7486_2_pin8,
       _7486_2_pin11, _74283_1_pin7;

  _7486 _7486_1 (
    .pin1(b3), .pin2(Subtract), .pin3(_7486_1_pin3), .pin4(b2), .pin5(Subtract), .pin6(_7486_1_pin6),
    .pin7(1'b0), .pin8(_7486_1_pin8), .pin9(Subtract), .pin10(b6), .pin11(_7486_1_pin11), .pin12(Subtract),
    .pin13(b7), .pin14(1'b1));
  _7486 _7486_2 (
    .pin1(b1), .pin2(Subtract), .pin3(_7486_2_pin3), .pin4(b0), .pin5(Subtract), .pin6(_7486_2_pin6),
    .pin7(1'b0), .pin8(_7486_2_pin8), .pin9(Subtract), .pin10(b4), .pin11(_7486_2_pin11), .pin12(Subtract),
    .pin13(b5), .pin14(1'b1));
  _74283 _74283_1 (
    .pin1(c5), .pin2(_7486_2_pin11), .pin3(a5), .pin4(c4), .pin5(a4), .pin6(_7486_2_pin8),
    .pin7(_74283_1_pin7), .pin8(1'b0), .pin10(c7), .pin11(_7486_1_pin11), .pin12(a7), .pin13(c6), .pin14(a6),
    .pin15(_7486_1_pin8), .pin16(1'b1));  // open: pin9
  _74283 _74283_2 (
    .pin1(c1), .pin2(_7486_2_pin3), .pin3(a1), .pin4(c0), .pin5(a0), .pin6(_7486_2_pin6), .pin7(Subtract),
    .pin8(1'b0), .pin9(_74283_1_pin7), .pin10(c3), .pin11(_7486_1_pin3), .pin12(a3), .pin13(c2), .pin14(a2),
    .pin15(_7486_1_pin6), .pin16(1'b1));

  // Notes on the sheet:
  //   A
  //   B
  //   Add/Subtract
  //   ALU Output
endmodule
