// Digital circuit ALU_logic_diagram.dig as structural Verilog
module ALU_logic_diagram (
  input  b0,
  input  b1,
  input  b2,
  input  b3,
  input  b4,
  input  b5,
  input  b6,
  input  b7,
  input  Subtract,
  input  a0,
  input  a1,
  input  a2,
  input  a3,
  input  a4,
  input  a5,
  input  a6,
  input  a7,
  output c7,
  output c6,
  output c5,
  output c4,
  output c3,
  output c2,
  output c1,
  output c0
);

  wire _74283_1_pin2, _74283_1_pin6, _74283_1_pin7, _74283_1_pin11, _74283_1_pin15, _74283_2_pin2,
       _74283_2_pin6, _74283_2_pin11, _74283_2_pin15;

  _74283 _74283_1 (
    .pin1(c5), .pin2(_74283_1_pin2), .pin3(a5), .pin4(c4), .pin5(a4), .pin6(_74283_1_pin6),
    .pin7(_74283_1_pin7), .pin8(1'b0), .pin10(c7), .pin11(_74283_1_pin11), .pin12(a7), .pin13(c6),
    .pin14(a6), .pin15(_74283_1_pin15), .pin16(1'b1));  // open: pin9
  _74283 _74283_2 (
    .pin1(c1), .pin2(_74283_2_pin2), .pin3(a1), .pin4(c0), .pin5(a0), .pin6(_74283_2_pin6), .pin7(Subtract),
    .pin8(1'b0), .pin9(_74283_1_pin7), .pin10(c3), .pin11(_74283_2_pin11), .pin12(a3), .pin13(c2),
    .pin14(a2), .pin15(_74283_2_pin15), .pin16(1'b1));
  xor xor_1 (_74283_1_pin11, b7, Subtract);
  xor xor_2 (_74283_1_pin15, b6, Subtract);
  xor xor_3 (_74283_1_pin2, b5, Subtract);
  xor xor_4 (_74283_1_pin6, Subtract, b4);
  xor xor_5 (_74283_2_pin11, b3, Subtract);
  xor xor_6 (_74283_2_pin15, Subtract, b2);
  xor xor_7 (_74283_2_pin2, Subtract, b1);
  xor xor_8 (_74283_2_pin6, Subtract, b0);

  // Notes on the sheet:
  //   A
  //   ALU Output
  //   B
  //   Add/Subtract
endmodule
